# Fritzing sketch Fishda (saved by Fritzing 0.9.3b)
breadboards: 1

parts:
  Part1 = Arduino Uno (Rev3)
  Part2 = Arduino Leonardo (Rev3b)
  Part4 = MicroSD Card Module
  SP1 = SPEAKER [package=pcb_mount_speaker]
  hc-sr1 = hc-sr04
  J1 = Basic Servo
  M1 = DC Motor  # not connected
  LED1 = LED - 5mm [color="Red (633nm)" package="5 mm [THT]"]
  LED2 = LED - 5mm [color="Red (633nm)" package="5 mm [THT]"]  # not connected
  LED3 = LED - 5mm [color="Red (633nm)" package="5 mm [THT]"]  # not connected
  LED4 = LED - 5mm [color="Red (633nm)" package="5 mm [THT]"]  # not connected
  R1 = Resistor [tolerance=±5% resistance=220 package="2010 [SMD]"]
  Part5 = Arduino Motor Shield
  U1 = LM386 [package=dip08]  # not connected
  M2 = DC Motor  # not connected

nets:
  N1: Part1.D8, Part2.D8/A8
  N2: Part1.D9_PWM, SP1.-
  N3: Part1.D10_PWM/SS, Part4.CS
  N4: Part1.D11_PWM/MOSI, Part4.MOSI
  N5: Part1.D12/MISO, Part4.MISO
  N6: Part1.D13/SCK, Part4.SCK
  N7: Part1.D2, Part2.D2/SDA
  N8: Part1.D3_PWM, Part2.D3_PWM/SCL
  N9: Part1.D4, Part2.D4/A6
  N10: Part1.D5_PWM, J1.pulse
  N11: Part1.D6_PWM, hc-sr1.Trig
  N12: Part1.D7, hc-sr1.Echo
  GND: Part1.GND, Part2.GND, Part4.GND, SP1.+, hc-sr1.GND, J1.gnd, R1.Pin_1
  VCC: Part1.VIN, Part2.5V, Part4.VCC, hc-sr1.VCC, J1.vcc
  N13: Part2.D5_PWM, LED1.anode
  N14: Part2.D9_PWM/A9, Part5.D9
  N15: Part2.D10_PWM/A10, Part5.D10
